# Fritzing sketch sketch01-nt0yg2n2 (saved by Fritzing 0.9.6b)
breadboards: 1

parts:
  Part1 = Arduino Mega ADK (Rev3)
  J1 = Piezo Speaker
  LED1 = smd LED [color="Red (633nm)" package="1206 [SMD]"]
  LED2 = smd LED [color="Orange (612nm)" package="0603 [SMD]"]
  LED3 = smd LED [color="Yellow (595nm)" package="0603 [SMD]"]
  LED4 = smd LED [color="Blue (525nm)" package="0603 [SMD]"]
  Mod1 = KY-018 Photoresistor Module [package="Breakout board"]
  PIR1 = PIR sensor
  7SEG1 = 7-Segment LED I2C Backpack (yellow)
  Part2 = Matrix LED de 8x8 basada en MAX7219
  LED5 = smd LED [color="White (4500K)" package="0603 [SMD]"]
  Part3 = 12 NeoPixel Ring [part_number=1643]  # not connected

nets:
  N1: Part1.D10_PWM, LED5.anode
  N2: Part1.D9_PWM, LED1.anode
  N3: Part1.D8_PWM, LED3.anode
  5V: Part1.5V, PIR1.VDD, 7SEG1.V+
  GND: Part1.GND, J1.pin1, LED1.cathode, LED2.cathode, LED3.cathode, LED4.cathode, Mod1.-, PIR1.GND, 7SEG1.GND, Part2.GND, LED5.cathode
  N4: Part1.D6_PWM, LED4.anode
  N5: Part1.D7_PWM, LED2.anode
  N6: Part1.D36, 7SEG1.SDA
  N7: Part1.D38, 7SEG1.SCL
  N8: Part1.D40, PIR1.SIG
  N9: Part1.D42, Mod1.S
  N10: Part1.D44, J1.pin2
  N11: Part1.D46, Part2.CLK
  N12: Part1.D48, Part2.CS
  N13: Part1.D50/MISO, Part2.DIN

custom parts:
  KY-018 Photoresistor Module: KY-018 Photoresistor module, used to measure light intensity. It can determine the presence or absence of light.
  7-Segment LED I2C Backpack (yellow): 4-digit, 7-segment LED Display with I2C Control
  12 NeoPixel Ring: 12 ultra bright smart LED NeoPixels are arranged in a circle with 1.5" (37mm) outer diameter. The rings are 'chainable' - connect the output pin of one to the input pin of another. Use only one microcontroller pin to control as many as you can chain together! Each LED is addressable as the driver chip is inside the LED. Each one has ~18mA constant current drive so the color will be very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
